# Fritzing sketch CoronaAiringStation (saved by Fritzing 0.9.6b)
breadboards: 1

parts:
  Part1 = Arduino Uno (Rev3)
  R1 = Resistor [tolerance=±5% resistance=10k package=THT]
  J1 = Piezo Speaker
  S2 = Pushbutton [package="[THT]"]
  M1 = Humidity and Temperature Sensor DHT11
  R2 = Resistor [tolerance=±5% resistance=10k package=THT]

nets:
  N1: Part1.D8, J1.pin2
  N2: Part1.D2, M1.Data, R2.Pin_1
  N3: Part1.D3_PWM, R1.Pin_1, S2.Pin_1, S2.Pin_2
  3V3: Part1.3V3, M1.Vcc, R2.Pin_0
  N4: Part1.5V, S2.Pin_3, S2.Pin_4
  GND: Part1.GND, R1.Pin_0, J1.pin1, M1.GND

custom parts:
  Humidity and Temperature Sensor DHT11: Digital relative humidity & temperature sensor DHT11

// code stored in the sketch: CoronaAiringStation.ino

